// Logisim project cpu.circ as structural Verilog: 4 circuits, main circuit main
module main (
  input  [15:0] INSTRUCTION,
  input  CLOCK,
  output [15:0] FETCH_ADDRESS,
  output [15:0] L_s0_Value_555821f6,
  output [15:0] L_s1_Value_bb868b5b,
  output [15:0] L_s2_Value_1029e135,
  output [15:0] L_ra_Value_3ae5280b,
  output [15:0] L_sp_Value_256d6ed0,
  output [15:0] L_HI_Value_4d3aacc1,
  output [15:0] L_LO_Value_6d74149f
);

  wire controller_1_clk_out1, controller_1_clk_out2, controller_1_we_reg;
  wire [2:0] instruction_decoder_1_funct, instruction_decoder_1_rd, instruction_decoder_1_rs,
       instruction_decoder_1_rt, multiplexer_1_out;
  wire [3:0] instruction_decoder_1_opcode;
  wire [9:0] instruction_decoder_1_immediate;
  wire [15:0] adder_4_1_pc_out, ALU_R1, ALU_R2, bit_extender_1_out, main_1_read_data_1_d638ea5b,
       main_1_read_data_2_45f3f23e, multiplexer_2_out, multiplexer_3_out;

  Register #(.width(16)) L_PC_1fb09d07 (.D(adder_4_1_pc_out), .en(1'b1), .clk(CLOCK), .Q(FETCH_ADDRESS));  // open: clr
  Adder_4 adder_4_1 (.PC_in(FETCH_ADDRESS), .PC_out(adder_4_1_pc_out));
  Controller controller_1 (
    .opcode(instruction_decoder_1_opcode), .funct(instruction_decoder_1_funct), .WE_REG(controller_1_we_reg),
    .clk_in(CLOCK), .clk_out1(controller_1_clk_out1), .clk_out2(controller_1_clk_out2));  // open: S_ALU
  Instruction_decoder instruction_decoder_1 (
    .rs(instruction_decoder_1_rs), .Instruction(INSTRUCTION), .rt(instruction_decoder_1_rt),
    .rd(instruction_decoder_1_rd), .immediate(instruction_decoder_1_immediate),
    .funct(instruction_decoder_1_funct), .opcode(instruction_decoder_1_opcode));
  Multiplexer #(.width(3), .enable("false")) multiplexer_1 (
    .in0(instruction_decoder_1_rt), .in1(instruction_decoder_1_rd), .out(multiplexer_1_out));  // open: sel
  assign bit_extender_1_out = {{6{instruction_decoder_1_immediate[9]}}, instruction_decoder_1_immediate};  // Bit_Extender bit_extender_1
  regfile_main main_1 (
    .Read_Register_1_a0c8cd62(instruction_decoder_1_rs), .Read_Register_2_6a35ea3b(multiplexer_1_out),
    .Write_Register_a5712683(instruction_decoder_1_rd), .Write_Data_73679b02(ALU_R1),
    .Write_Enable_cb4a62c6(controller_1_we_reg), .Clock(controller_1_clk_out1),
    .Read_Data_1_d638ea5b(main_1_read_data_1_d638ea5b), .Read_Data_2_45f3f23e(main_1_read_data_2_45f3f23e),
    .L_s0_Value_319056dc(L_s0_Value_555821f6), .L_s1_Value_178742e2(L_s1_Value_bb868b5b),
    .L_s2_Value_c4d9ac04(L_s2_Value_1029e135), .L_ra_Value_229931e7(L_ra_Value_3ae5280b),
    .L_sp_Value_102b2bfe(L_sp_Value_256d6ed0));
  Multiplexer #(.width(16), .enable("false")) multiplexer_2 (
    .in0(main_1_read_data_1_d638ea5b), .in1(bit_extender_1_out), .out(multiplexer_2_out));  // open: sel
  alu_main main_2 (
    .X(multiplexer_2_out), .Result(ALU_R1), .Y(multiplexer_3_out), .Result_2_c6eb2740(ALU_R2));  // open: Switch, Equal
  Multiplexer #(.select(2), .width(16), .enable("false")) multiplexer_3 (
    .in0(main_1_read_data_2_45f3f23e), .in1(16'h6), .in2(bit_extender_1_out), .out(multiplexer_3_out));  // open: in3, sel
  mem_main MEM (.Clock(controller_1_clk_out2));  // open: Address, Write_Data, Write_En, Read_Data
  Register #(.width(16)) L_HI_108849eb (
    .D(ALU_R2), .en(1'b1), .clk(controller_1_clk_out2), .Q(L_LO_Value_6d74149f));  // open: clr
  Register #(.width(16)) L_LO_6db75bec (
    .D(ALU_R1), .en(1'b1), .clk(controller_1_clk_out2), .Q(L_HI_Value_4d3aacc1));  // open: clr

  // Other names for the same wires on the sheet: clk = CLOCK; fetch_addr[15:0] = FETCH_ADDRESS;
  //   HI[15:0] = L_LO_Value_6d74149f; LO[15:0] = L_HI_Value_4d3aacc1; ra[15:0] = L_ra_Value_3ae5280b;
  //   s0[15:0] = L_s0_Value_555821f6; s1[15:0] = L_s1_Value_bb868b5b; s2[15:0] = L_s2_Value_1029e135;
  //   sp[15:0] = L_sp_Value_256d6ed0

  // Notes on the sheet:
  //   Output
  //   These are outputs/inputs from run.circ
  //   Inputs
  //   These are DEBUG/TEST outputs from your circuit.
endmodule

module Adder_4 (
  input  [15:0] PC_in,
  output [15:0] PC_out
);

  Adder #(.width(16)) adder_1 (.a(PC_in), .b(16'h2), .out(PC_out));  // open: cin, cout
endmodule

module Instruction_decoder (
  input  [15:0] Instruction,
  output [2:0] funct,
  output [2:0] rt,
  output [2:0] rs,
  output [9:0] immediate,
  output [2:0] rd,
  output [3:0] opcode
);


  assign funct = Instruction[2:0];
  assign immediate = Instruction[9:0];
  assign opcode = Instruction[15:12];
  assign rd = Instruction[11:9];
  assign rs = Instruction[8:6];
  assign rt = Instruction[5:3];
endmodule

module Controller (
  input  [2:0] funct,
  input  [3:0] opcode,
  input  clk_in,
  output [2:0] S_ALU,
  output clk_out1,
  output clk_out2,
  output WE_REG
);

  Multiplexer #(.select(4), .width(3), .enable("false")) multiplexer_1 (
    .in0(funct), .out(S_ALU), .sel(opcode));  // open: in1, in2, in3, in4, in5, in6, in7, in8, in9, in10, in11, in12, in13, in14, in15
  nand nand_1 (WE_REG, funct[0], funct[1], funct[2]);

  assign clk_out1 = clk_in;
  assign clk_out2 = clk_in;
endmodule
